# Fritzing sketch Home+ (saved by Fritzing 0.9.3b)
breadboards: 1

parts:
  U1 = ESP32-38PinWide [part_number=ESP32-38PinWide]
  Mod1 = KY-019 5V Relay Module [package="Breakout board"]
  BULB1 = Incandescent light bulb small [package="bulb sm"]
  M1 = DC Motor
  Mod2 = KY-019 5V Relay Module [package="Breakout board"]
  J1 = 120V duplex outlet_1  # not connected
  J2 = 220v plug
  Part1 = Lilypad Battery Connect  # not connected
  J3 = 220v plug
  Part2 = Lilypad Battery Connect  # not connected

nets:
  N1: U1.3.3, Mod1.+, Mod2.+
  N2: U1.GPIO11, Mod1.-, Mod2.-
  N3: U1.GPIO7, Mod1.S
  N4: U1.GPIO8, Mod2.S
  N5: Mod1.NC, J2.pin1
  N6: Mod1.Common, BULB1.1
  N7: BULB1.2, J2.pin2
  N8: M1.pin_1, Mod2.Common
  N9: M1.pin_2, J3.pin2
  N10: Mod2.NC, J3.pin1

notes:
  Light
  Home Gate(Motors)

custom parts:
  ESP32-38PinWide: Generic 38-Pin ESP32 with wide format (only access to one side of pins on a breadboard) based on Stephen Lilley's HiLetgo ESP-WROOM-32 ESP32 ESP-32S Development Board.
  KY-019 5V Relay Module: KY-019 5V Relay module, used to control AC circuits. (Special thanks to vanepp for fixing the PCB holes and other errors)
  120V duplex outlet_1: 120V duplex outlet.
  220v plug: Generic 220V AC plug.
